# Fritzing sketch projeto-01 (saved by Fritzing 0.9.3b)
breadboards: 1

parts:
  Componente1 = Arduino Uno (Rev3)
  LED1 = smd LED [color="Red (633nm)" package="0603 [SMD]"]

nets:
  N1: Componente1.D13/SCK, LED1.anode
  N2: Componente1.GND, LED1.cathode
