# Fritzing sketch projeto-02 (saved by Fritzing 0.9.3b)
breadboards: 1

parts:
  Componente1 = Arduino Uno (Rev3)
  DHT2 = DHT11 Humitidy and Temperature Sensor
  LDR1 = Photocell (LDR) [package=THT]
  R3 = Resistor [tolerance=±5% resistance=220 package=THT]

nets:
  N1: Componente1.A0, DHT2.DATA
  N2: Componente1.A1, LDR1.pin_0, R3.Pin_0
  5V: Componente1.5V, DHT2.VDD, LDR1.pin_1
  GND: Componente1.GND, DHT2.GND, R3.Pin_1

custom parts:
  DHT11 Humitidy and Temperature Sensor: DHT11 Humidity and Temperature Sensor
